# Fritzing sketch infrared_sensor (saved by Fritzing 0.9.3b)
breadboards: 1

parts:
  Onderdeel1 = Arduino Uno (Rev3)
  R1 = Resistor [tolerance=±5% resistance=220 package="0603 [SMD]"]
  LED1 = LEDs [package=led10mm]
  M1 = fc-51 [package=THT]

nets:
  N1: Onderdeel1.D8, M1.pin1
  N2: Onderdeel1.GND, R1.Pin_1, M1.pin2
  N3: Onderdeel1.D7, LED1.C
  N4: Onderdeel1.5V, M1.pin3
  N5: R1.Pin_0, LED1.A

// code stored in the sketch: Untitled.ino
#define irObstaclePin 8  // This is our input pin
#define led 7
int Obstacle = HIGH;  // HIGH MEANS NO OBSTACLE
void setup() 
{
 pinMode(irObstaclePin, INPUT);
 pinMode(led, OUTPUT);
 Serial.begin(9600);
}
void loop() 
{
 Obstacle = digitalRead(irObstaclePin);
 if (Obstacle == LOW)
 {
   Serial.println("OBSTACLE!!, OBSTACLE!!");  
   digitalWrite(led, LOW);
 }
 else
 {
   Serial.println("clear");
   digitalWrite(led, LOW);
 }
 delay(200);
}
