# Fritzing sketch lift_etageX (saved by Fritzing 0.9.3b)
breadboards: 1

parts:
  M1 = fc-51 [package=THT]
  Onderdeel1 = Arduino Uno (Rev3)
  IC1 = SHIFT REGISTER [package=dil16]
  R1 = Resistor [tolerance=±5% resistance=220 package="0603 [SMD]"]
  S1 = Pushbutton [package="[THT]"]
  S2 = Pushbutton [package="[THT]"]
  LED1 = smd LED [color="Red (633nm)" package="1206 [SMD]"]
  LED2 = smd LED [color="Red (633nm)" package="1206 [SMD]"]
  R2 = Resistor [tolerance=±5% resistance=220 package="2512 [SMD]"]
  R3 = Resistor [tolerance=±5% resistance=220 package="0603 [SMD]"]
  LED3 = smd LED [color="Red (633nm)" package="1206 [SMD]"]
  DI1 = 7-Segment LED Display [package=THT]

nets:
  N1: M1.pin1, Onderdeel1.D7
  N2: M1.pin2, Onderdeel1.GND, IC1.G, LED1.cathode, LED2.cathode, LED3.cathode
  N3: M1.pin3, Onderdeel1.5V, R1.Pin_1
  N4: Onderdeel1.D8, IC1.SCK
  N5: Onderdeel1.D11_PWM/MOSI, IC1.RCK
  N6: Onderdeel1.D12/MISO, IC1.SER
  N7: Onderdeel1.D2, S2.Pin_1, S2.Pin_2, LED1.anode
  N8: Onderdeel1.D4, S1.Pin_3, S1.Pin_4, LED2.anode
  N9: Onderdeel1.D5_PWM, R3.Pin_0
  N10: IC1.QB, DI1.cathodeG
  N11: IC1.QC, DI1.cathodeF
  N12: IC1.QD, DI1.cathodeE
  N13: IC1.QE, DI1.cathodeD
  N14: IC1.QF, DI1.cathodeC
  N15: IC1.QG, DI1.cathodeA
  N16: IC1.QH, DI1.cathodeB
  N17: IC1.GND, IC1.SCL, R1.Pin_0, R2.Pin_0
  N18: IC1.QA, DI1.cathodeDP
  N19: IC1.VCC, DI1.commAnode#7
  N20: S1.Pin_1, S1.Pin_2, S2.Pin_3, S2.Pin_4, R2.Pin_1
  N21: R3.Pin_1, LED3.anode

// code stored in the sketch: Lift.ino

const int latchPin = 12;//Pin connected to ST_CP of 74HC595
const int clockPin = 8;//Pin connected to SH_CP of 74HC595
const int dataPin = 11; //Pin connected to DS of 74HC595

#define led_lift 5

#define knopl 4
#define knopr 2

int buttonstate_l = LOW;
int buttonstate_r = LOW;

#define irObstaclePin 7  // This is our input pin

int waar;

int Obstacle = HIGH;
/*=======================================================================================================
  //display 0,1,2,3,4,5,6,7,8
  Number 0 :  00000011     3
  Number 1 :  10101111     159
  Number 2 :  00100101     37
  Number 3 :  00001101     13
  Number 4 :  10011001     153
  Number 5 :  01001001     73
  Number 6 :  01000001     65
  Number 7 :  00011111     31
  Number 8 :  00000001     1

  To display the dot, simply subtract 1.
  example : 1 - 1 = 0  or b0000000 0x0 to display 8
*/
/*In order to display zero your array has decimal number 3. However using the shift register
  it is actuall the binary number that is uploaded into the resitsre: zie the table above for zero: 00000011.
*/
int datArray[9] = {2, 158, 36, 12, 152, 72, 64, 30, 0}; // array without the decimal

void setup ()

{
  //set pins to output
  Serial.begin(9600);

  pinMode(irObstaclePin, INPUT);
  pinMode(knopr, INPUT);
  pinMode(knopl, INPUT);
  
  pinMode(led_lift, OUTPUT);
  
  pinMode(latchPin, OUTPUT);
  pinMode(clockPin, OUTPUT);
  pinMode(dataPin, OUTPUT);
}
void loop()


{
  Obstacle = digitalRead(irObstaclePin);
  buttonstate_l = digitalRead(knopl);
  buttonstate_r = digitalRead(knopr);

  /*
    Serial.print("r");
    Serial.println(buttonstate_r);
    Serial.print("l");
    Serial.println(buttonstate_l);
  */

  



  if (Obstacle == LOW) {
    waar = 1 ;
    digitalWrite(led_lift, HIGH);
    Serial.println("OBSTACLE!!, OBSTACLE!!");  

    digitalWrite(latchPin, LOW);
    shiftOut(dataPin, clockPin, MSBFIRST, 159);
    digitalWrite(latchPin, HIGH);

  } else {
    waar = 1 ;
    digitalWrite(led_lift, LOW);

    digitalWrite(latchPin, LOW);
    shiftOut(dataPin, clockPin, MSBFIRST, 3);
    digitalWrite(latchPin, HIGH);
    Serial.println("clear");
  }

}
